// Digital circuit Instruction Decoder.dig as structural Verilog
module Instruction_Decoder (
  input  CLK,
  input  I0,
  input  I1,
  input  I2,
  input  I3,
  input  I4,
  input  I5,
  input  I6,
  input  I7,
  output ALUE,
  output ALU_B,
  output ALUC,
  output ALUS,
  output ALUADD,
  output ALUAND,
  output ALUOR,
  output ALUNOT,
  output ALUXOR,
  output ALUSL,
  output ALUSR,
  output ALURL,
  output ALURR,
  output ALUMULT,
  output ALUDIV,
  output AR,
  output AW,
  output XR,
  output XW,
  output YR,
  output YW,
  output ZR,
  output ZW,
  output PCE,
  output PCHR,
  output PCHW,
  output PCLR,
  output PCLW,
  output SPR,
  output SPW,
  output SPINC,
  output SPDEC,
  output OHR,
  output OHW,
  output OLR,
  output OLW,
  output MAWL,
  output MAWH,
  output SCF,
  output CCF,
  output SIMF,
  output CIMF,
  output IRQO,
  output INTACK,
  output HLT,
  output MR,
  output MW
);

  wire not_1_out;
  wire [13:0] counter_1_out;
  wire [47:47] undriven;

  not not_1 (not_1_out, CLK);
  Counter #(.Bits(3)) counter_1 (
    .en(not_1_out), .C(not_1_out), .clr(undriven[47]), .out(counter_1_out[2:0]));  // open: ovf
  ROM #(.AddrBits(14), .Bits(32)) rom_1 (
    .A({counter_1_out[13:11], I7, I6, I5, I4, I3, I2, I1, I0, counter_1_out[2:0]}), .sel(1'b1),
    .D({SPDEC, SPINC, SPW, SPR, PCLW, PCLR, PCHW, PCHR, PCE, ZW, ZR, YW, YR, XW, XR, AW, AR, ALUDIV, ALUMULT, ALURR, ALURL, ALUSR, ALUSL, ALUXOR, ALUNOT, ALUOR, ALUAND, ALUADD, ALUS, ALUC, ALU_B, ALUE}));
  // Pins of 11 and 14 bits meet at {counter_1_out[13:11], I7, I6, I5, I4, I3, I2, I1, I0, counter_1_out[2:0]}
  // Pins of 32 and 48 bits meet at {undriven[47], HLT, INTACK, IRQO, CIMF, SIMF, CCF, SCF, MW, MR, MAWH, MAWL, OLW, OLR, OHW, OHR, SPDEC, SPINC, SPW, SPR, PCLW, PCLR, PCHW, PCHR, PCE, ZW, ZR, YW, YR, XW, XR, AW, AR, ALUDIV, ALUMULT, ALURR, ALURL, ALUSR, ALUSL, ALUXOR, ALUNOT, ALUOR, ALUAND, ALUADD, ALUS, ALUC, ALU_B, ALUE}
endmodule
